// Logisim project AND_GATE.circ as structural Verilog: 30 circuits, main circuit ANDMLTG
module ANDMLTG (
  input  A,
  input  B,
  output out
);

  wire nand_1_out;

  nand nand_1 (nand_1_out, A, B);
  not not_1 (out, nand_1_out);

  // Notes on the sheet:
  //   notAB
endmodule

module NOT (
  input  a,
  output out
);

  nand nand_1 (out, a, a);

  // Notes on the sheet:
  //   ingresa el mismo valor a en los dos parametros
endmodule

module OR (
  input  a,
  input  b,
  output out
);

  wire not_1_out, not_2_out;

  not not_1 (not_1_out, a);
  not not_2 (not_2_out, b);
  nand nand_1 (out, not_1_out, not_2_out);

  // Notes on the sheet:
  //   notA
  //   notB
endmodule

module XOR (
  input  a,
  input  b,
  output out
);

  wire AND_2_out, AND_out, not_1_out, not_2_out;

  not not_1 (not_1_out, a);
  not not_2 (not_2_out, b);
  and AND (AND_out, a, not_2_out);
  and AND_2 (AND_2_out, not_1_out, b);
  or or_1 (out, AND_out, AND_2_out);

  // Notes on the sheet:
  //   A
  //   notA
  //   notB
  //   B
endmodule

module DMUX (
  input  sel,
  input  in,
  output a,
  output b
);

  wire notSel_out;

  not notSel (notSel_out, sel);
  and AND (a, notSel_out, in);
  and AND_2 (b, sel, in);
endmodule

module MUX (
  input  b,
  input  sel,
  input  a,
  output out
);

  wire AND_2_out, AND_3_out, AND_4_out, AND_out, notA_out, notB_out, notSel_out, OR_out;

  not notB (notB_out, b);
  not notSel (notSel_out, sel);
  and AND (AND_out, notB_out, notSel_out);
  or OR (OR_out, b, AND_out);
  not notA (notA_out, a);
  and AND_2 (AND_2_out, OR_out, a);
  and AND_3 (AND_3_out, notA_out, b);
  and AND_4 (AND_4_out, AND_3_out, sel);
  or OR_2 (out, AND_2_out, AND_4_out);

  // Notes on the sheet:
  //   bro haz primero los parentesis !
endmodule

module ejemplo (
  input  x,
  input  y,
  input  z,
  output out_4
);

  wire AND_out, not_1_out, OR_out;

  not not_1 (not_1_out, y);
  or OR (OR_out, not_1_out, y);
  and AND (AND_out, x, OR_out);
  and AND_2 (out_4, AND_out, y);

  assign z = y;
endmodule

module MUX_SIMPLIFIED (
  input  a,
  input  sel,
  input  b,
  output out_4
);

  wire AND_2_out, AND_out, notSEL_out;

  not notSEL (notSEL_out, sel);
  and AND (AND_out, sel, b);
  and AND_2 (AND_2_out, a, notSEL_out);
  or OR (out_4, AND_2_out, AND_out);
endmodule

module _16_bitNot (
  input  [15:0] IN,
  output [15:0] OUT
);

  assign OUT[3:0] = ~IN[3:0];  // NOT_Gate not_1, 4 bits wide
  assign OUT[7:4] = ~IN[7:4];  // NOT_Gate not_2, 4 bits wide
  assign OUT[11:8] = ~IN[11:8];  // NOT_Gate not_3, 4 bits wide
  assign OUT[15:12] = ~IN[15:12];  // NOT_Gate not_4, 4 bits wide

  // Notes on the sheet:
  //   SE ELIGE EN BITS DE DATOS: 16 
endmodule

module AND16 (
  input  [15:0] a,
  input  [15:0] b,
  output [15:0] out
);

  assign out[3:0] = a[3:0] & b[3:0];  // AND_Gate and_1, 4 bits wide
  assign out[7:4] = a[7:4] & b[7:4];  // AND_Gate and_2, 4 bits wide
  assign out[11:8] = a[11:8] & b[11:8];  // AND_Gate and_3, 4 bits wide
  assign out[15:12] = a[15:12] & b[15:12];  // AND_Gate and_4, 4 bits wide
endmodule

module OR16 (
  input  [15:0] a,
  input  [15:0] b,
  output [15:0] out
);

  assign out[15:8] = a[15:8] | b[15:8];  // OR_Gate or_1, 8 bits wide
  assign out[7:0] = a[7:0] | b[7:0];  // OR_Gate or_2, 8 bits wide
endmodule

module MUX16 (
  input  [15:0] a,
  input  [15:0] b,
  input  sel,
  output [15:0] out
);

  Multiplexer #(.width(16), .enable("false")) multiplexer_1 (.in0(a), .in1(b), .out(out), .sel(sel));

  // Notes on the sheet:
  //   en el mux hay un enable, ten en cuenta
endmodule

module _0R8WAY (
  input  in_1,
  input  in_2,
  input  in_3,
  input  in_4,
  input  in_5,
  input  in_6,
  input  in_7,
  input  in_8,
  output out_9
);

  wire or_1_out, or_2_out, or_3_out, or_4_out, or_5_out, or_6_out;

  or or_1 (or_1_out, in_1, in_2);
  or or_2 (or_2_out, or_1_out, in_3);
  or or_3 (or_3_out, or_2_out, in_4);
  or or_4 (or_4_out, or_3_out, in_5);
  or or_5 (or_5_out, or_4_out, in_6);
  or or_6 (or_6_out, or_5_out, in_7);
  or or_7 (out_9, or_6_out, in_8);
endmodule

module DMUX4 (
  input  IN,
  input  SEL_1,
  input  SEL_0,
  output A,
  output B,
  output C,
  output D
);

  wire demultiplexer_1_out0, demultiplexer_1_out1;

  Demultiplexer #(.enable("false")) demultiplexer_1 (
    .out0(demultiplexer_1_out0), .out1(demultiplexer_1_out1), .in(IN), .sel(SEL_1));
  Demultiplexer #(.enable("false")) demultiplexer_2 (.out0(A), .out1(B), .in(demultiplexer_1_out0), .sel(SEL_0));
  Demultiplexer #(.enable("false")) demultiplexer_3 (.out0(C), .out1(D), .in(demultiplexer_1_out1), .sel(SEL_0));
endmodule

module DMUX8 (
  input  IN,
  input  SEL_1,
  input  SEL_0,
  input  SEL_2,
  output A,
  output B,
  output C,
  output D,
  output E,
  output F,
  output G,
  output H
);

  wire demultiplexer_1_out0, demultiplexer_1_out1, demultiplexer_2_out0, demultiplexer_2_out1,
       demultiplexer_3_out0, demultiplexer_3_out1;

  Demultiplexer #(.enable("false")) demultiplexer_1 (
    .out0(demultiplexer_1_out0), .out1(demultiplexer_1_out1), .in(IN), .sel(SEL_2));
  Demultiplexer #(.enable("false")) demultiplexer_2 (
    .out0(demultiplexer_2_out0), .out1(demultiplexer_2_out1), .in(demultiplexer_1_out0), .sel(SEL_1));
  Demultiplexer #(.enable("false")) demultiplexer_3 (
    .out0(demultiplexer_3_out0), .out1(demultiplexer_3_out1), .in(demultiplexer_1_out1), .sel(SEL_1));
  Demultiplexer #(.enable("false")) demultiplexer_4 (.out0(A), .out1(B), .in(demultiplexer_2_out0), .sel(SEL_0));
  Demultiplexer #(.enable("false")) demultiplexer_5 (.out0(C), .out1(D), .in(demultiplexer_2_out1), .sel(SEL_0));
  Demultiplexer #(.enable("false")) demultiplexer_6 (.out0(E), .out1(F), .in(demultiplexer_3_out0), .sel(SEL_0));
  Demultiplexer #(.enable("false")) demultiplexer_7 (.out0(G), .out1(H), .in(demultiplexer_3_out1), .sel(SEL_0));
endmodule

module MUX8W16 (
  input  [15:0] A,
  input  [15:0] B,
  input  [15:0] C,
  input  SEL_1,
  input  [15:0] D,
  input  SEL_0,
  input  SEL_2,
  input  [15:0] E,
  input  [15:0] F,
  input  [15:0] G,
  input  [15:0] H,
  output [15:0] OUT
);

  wire [15:0] multiplexer_1_out, multiplexer_2_out, multiplexer_3_out, multiplexer_4_out, multiplexer_5_out,
       multiplexer_6_out;

  Multiplexer #(.width(16), .enable("false")) multiplexer_1 (.in0(A), .in1(B), .out(multiplexer_1_out), .sel(SEL_0));
  Multiplexer #(.width(16), .enable("false")) multiplexer_2 (.in0(C), .in1(D), .out(multiplexer_2_out), .sel(SEL_0));
  Multiplexer #(.width(16), .enable("false")) multiplexer_3 (.in0(E), .in1(F), .out(multiplexer_3_out), .sel(SEL_0));
  Multiplexer #(.width(16), .enable("false")) multiplexer_4 (.in0(G), .in1(H), .out(multiplexer_4_out), .sel(SEL_0));
  Multiplexer #(.width(16), .enable("false")) multiplexer_5 (
    .in0(multiplexer_1_out), .in1(multiplexer_2_out), .out(multiplexer_5_out), .sel(SEL_1));
  Multiplexer #(.width(16), .enable("false")) multiplexer_6 (
    .in0(multiplexer_3_out), .in1(multiplexer_4_out), .out(multiplexer_6_out), .sel(SEL_1));
  Multiplexer #(.width(16), .enable("false")) multiplexer_7 (
    .in0(multiplexer_5_out), .in1(multiplexer_6_out), .out(OUT), .sel(SEL_2));
endmodule

module MUX4W16 (
  input  [15:0] A,
  input  [15:0] B,
  input  [15:0] in_3,
  input  SEL_1,
  input  [15:0] in_5,
  input  SEL_0,
  output [15:0] out_7
);

  wire [15:0] multiplexer_1_out, multiplexer_2_out;

  Multiplexer #(.width(16), .enable("false")) multiplexer_1 (.in0(A), .in1(B), .out(multiplexer_1_out), .sel(SEL_0));
  Multiplexer #(.width(16), .enable("false")) multiplexer_2 (
    .in0(in_3), .in1(in_5), .out(multiplexer_2_out), .sel(SEL_0));
  Multiplexer #(.width(16), .enable("false")) multiplexer_3 (
    .in0(multiplexer_1_out), .in1(multiplexer_2_out), .out(out_7), .sel(SEL_1));
endmodule

module DMUX4_5 (
  input  in,
  input  [1:0] SEL,
  output A,
  output B,
  output C,
  output D
);

  wire and_1_out, and_2_out, and_3_out, and_4_out, not_1_out, not_2_out;

  not not_1 (not_1_out, in);
  not not_2 (not_2_out, SEL[1]);
  and and_1 (and_1_out, in, not_2_out);
  and and_2 (and_2_out, in, not_2_out);
  and and_3 (and_3_out, in, SEL[1]);
  and and_4 (and_4_out, in, SEL[1]);
  and and_5 (A, and_1_out, not_1_out);
  and and_6 (B, and_2_out, not_1_out);
  and and_7 (C, and_3_out, in);
  and and_8 (D, and_4_out, in);

  assign SEL[0] = in;
endmodule

module ADDER (
  input  A,
  input  B,
  output sum,
  output carry
);

  xor xor_1 (sum, A, B);
  and and_1 (carry, A, B);

  // Notes on the sheet:
  //   CADA SALIDA TIENE SU PUERTA LOGICA , X+Y  ES XOR , MIENTRAS CARRY ES AND
endmodule

module HALF_ADDER (
  input  A,
  input  B,
  output sum
);

  xor xor_1 (sum, A, B);
endmodule

module FULL_ADDER (
  input  A,
  input  B,
  input  C,
  output sum,
  output carry
);

  wire and_1_out, and_2_out, and_3_out, and_4_out, not_1_out, not_2_out, xor_1_out;

  xor xor_1 (xor_1_out, B, C);
  not not_1 (not_1_out, A);
  and and_1 (and_1_out, not_1_out, xor_1_out);
  and and_2 (and_2_out, A, xor_1_out);
  and and_3 (and_3_out, B, C);
  or or_1 (carry, and_2_out, and_3_out);
  not not_2 (not_2_out, xor_1_out);
  and and_4 (and_4_out, not_2_out, A);
  or or_2 (sum, and_1_out, and_4_out);
endmodule

module ADD16_5 (
);

  FULL_ADDER full_adder_1 ();  // open: A, B, C, sum, carry
endmodule

module ADD16 (
  input  in_1,
  input  [15:0] A,
  input  [15:0] B,
  input  [15:0] in_4,
  input  A_2,
  input  A_3,
  input  A_4,
  input  B_2,
  input  A_5,
  input  A_6,
  input  A_7,
  input  B_3,
  input  B_4,
  input  [15:0] in_14,
  input  B_5,
  input  A_8,
  input  B_6,
  input  B_7,
  input  C,
  input  C_2,
  input  C_3,
  input  B_8,
  input  C_4,
  input  C_5,
  input  C_6,
  output [15:0] SUM,
  output CARRY,
  output sum_2,
  output sum_3,
  output sum_4,
  output sum_5,
  output sum_6,
  output sum_7,
  output sum_8,
  output sum_9,
  output sum_10,
  output sum_11,
  output sum_12,
  output sum_13,
  output sum_14,
  output sum_15,
  output carry_2,
  output carry_3,
  output carry_4,
  output carry_5,
  output carry_6,
  output carry_7,
  output carry_8
);

  wire add4_1_carry, add4_2_carry, add4_3_carry, and_1_out, and_2_out, and_3_out, and_4_out, and_5_out,
       and_6_out, and_7_out, and_8_out, and_9_out, and_10_out, and_11_out, and_12_out, and_13_out,
       and_14_out, and_15_out, and_16_out, and_17_out, and_18_out, and_19_out, and_20_out, and_21_out,
       and_22_out, and_23_out, and_24_out, and_25_out, and_26_out, and_27_out, and_28_out, and_29_out,
       and_30_out, and_31_out, and_32_out, and_33_out, and_34_out, and_35_out, and_36_out, and_37_out,
       and_38_out, and_39_out, and_40_out, and_41_out, and_42_out, and_43_out, and_44_out, and_45_out,
       and_46_out, and_47_out, and_48_out, and_49_out, and_50_out, and_51_out, and_52_out, and_53_out,
       and_54_out, and_55_out, and_56_out, not_1_out, not_2_out, not_3_out, not_4_out, not_5_out, not_6_out,
       not_7_out, not_8_out, not_9_out, not_10_out, not_11_out, not_12_out, not_13_out, not_14_out,
       not_15_out, not_16_out, not_17_out, not_18_out, not_19_out, not_20_out, not_21_out, not_22_out,
       not_23_out, not_24_out, not_25_out, not_26_out, not_27_out, not_28_out, or_1_out, or_3_out, or_5_out,
       or_7_out, or_9_out, or_11_out, or_13_out, xor_1_out, xor_3_out, xor_4_out, xor_5_out, xor_6_out,
       xor_7_out, xor_8_out, xor_9_out, xor_10_out, xor_11_out, xor_12_out, xor_13_out, xor_14_out;

  ADD4 add4_1 (.C(in_1), .A(A[3:0]), .B(B[3:0]), .SUM(SUM[3:0]), .CARRY(add4_1_carry));
  ADD4 add4_2 (.C(add4_1_carry), .A(A[7:4]), .B(B[7:4]), .SUM(SUM[7:4]), .CARRY(add4_2_carry));
  ADD4 add4_3 (.C(add4_2_carry), .A(A[11:8]), .B(B[11:8]), .SUM(SUM[11:8]), .CARRY(add4_3_carry));
  ADD4 add4_4 (.C(add4_3_carry), .A(A[15:12]), .B(B[15:12]), .SUM(SUM[15:12]), .CARRY(CARRY));
  xor xor_1 (xor_1_out, in_4[11], in_4[11]);
  not not_1 (not_1_out, in_4[11]);
  and and_1 (and_1_out, in_4[11], in_4[11]);
  and and_2 (and_2_out, not_1_out, xor_1_out);
  and and_3 (and_3_out, in_4[11], xor_1_out);
  or or_1 (or_1_out, and_3_out, and_1_out);
  not not_2 (not_2_out, xor_1_out);
  and and_4 (and_4_out, not_2_out, in_4[11]);
  or or_2 (sum_2, and_2_out, and_4_out);
  not not_3 (not_3_out, in_4[1]);
  xor xor_2 (in_4[11], in_4[11], or_1_out);
  and and_5 (and_5_out, in_4[1], in_4[11]);
  and and_6 (and_6_out, in_4[11], or_1_out);
  and and_7 (and_7_out, not_3_out, in_4[11]);
  not not_4 (not_4_out, in_4[11]);
  or or_3 (or_3_out, and_5_out, and_6_out);
  and and_8 (and_8_out, not_4_out, in_4[1]);
  or or_4 (sum_4, and_7_out, and_8_out);
  xor xor_3 (xor_3_out, in_4[11], or_3_out);
  not not_5 (not_5_out, in_4[2]);
  and and_9 (and_9_out, in_4[2], xor_3_out);
  and and_10 (and_10_out, in_4[11], or_3_out);
  and and_11 (and_11_out, not_5_out, xor_3_out);
  not not_6 (not_6_out, xor_3_out);
  or or_5 (or_5_out, and_9_out, and_10_out);
  and and_12 (and_12_out, not_6_out, in_4[2]);
  or or_6 (sum_3, and_11_out, and_12_out);
  xor xor_4 (xor_4_out, in_4[11], or_5_out);
  not not_7 (not_7_out, in_4[3]);
  and and_13 (and_13_out, in_4[3], xor_4_out);
  and and_14 (and_14_out, in_4[11], or_5_out);
  and and_15 (and_15_out, not_7_out, xor_4_out);
  not not_8 (not_8_out, xor_4_out);
  or or_7 (or_7_out, and_13_out, and_14_out);
  and and_16 (and_16_out, not_8_out, in_4[3]);
  or or_8 (sum_5, and_15_out, and_16_out);
  xor xor_5 (xor_5_out, in_4[11], or_7_out);
  not not_9 (not_9_out, in_4[4]);
  and and_17 (and_17_out, in_4[11], or_7_out);
  and and_18 (and_18_out, not_9_out, xor_5_out);
  not not_10 (not_10_out, xor_5_out);
  and and_19 (and_19_out, in_4[4], xor_5_out);
  or or_9 (or_9_out, and_19_out, and_17_out);
  and and_20 (and_20_out, not_10_out, in_4[4]);
  or or_10 (sum_8, and_18_out, and_20_out);
  xor xor_6 (xor_6_out, in_14[5], or_9_out);
  not not_11 (not_11_out, in_4[5]);
  and and_21 (and_21_out, not_11_out, xor_6_out);
  and and_22 (and_22_out, in_4[5], xor_6_out);
  and and_23 (and_23_out, in_14[5], or_9_out);
  or or_11 (or_11_out, and_22_out, and_23_out);
  not not_12 (not_12_out, xor_6_out);
  and and_24 (and_24_out, not_12_out, in_4[5]);
  or or_12 (sum_9, and_21_out, and_24_out);
  xor xor_7 (xor_7_out, in_14[6], or_11_out);
  not not_13 (not_13_out, in_4[6]);
  and and_25 (and_25_out, in_4[6], xor_7_out);
  and and_26 (and_26_out, in_14[6], or_11_out);
  and and_27 (and_27_out, not_13_out, xor_7_out);
  not not_14 (not_14_out, xor_7_out);
  or or_13 (or_13_out, and_25_out, and_26_out);
  and and_28 (and_28_out, not_14_out, in_4[6]);
  or or_14 (sum_6, and_27_out, and_28_out);
  xor xor_8 (xor_8_out, B_2, or_13_out);
  not not_15 (not_15_out, A_2);
  and and_29 (and_29_out, A_2, xor_8_out);
  and and_30 (and_30_out, B_2, or_13_out);
  and and_31 (and_31_out, not_15_out, xor_8_out);
  not not_16 (not_16_out, xor_8_out);
  or or_15 (carry_2, and_29_out, and_30_out);
  and and_32 (and_32_out, not_16_out, A_2);
  or or_16 (sum_7, and_31_out, and_32_out);
  xor xor_9 (xor_9_out, B_3, C);
  not not_17 (not_17_out, A_3);
  and and_33 (and_33_out, B_3, C);
  and and_34 (and_34_out, not_17_out, xor_9_out);
  not not_18 (not_18_out, xor_9_out);
  and and_35 (and_35_out, A_3, xor_9_out);
  or or_17 (carry_3, and_35_out, and_33_out);
  and and_36 (and_36_out, not_18_out, A_3);
  or or_18 (sum_10, and_34_out, and_36_out);
  not not_19 (not_19_out, A_6);
  xor xor_10 (xor_10_out, B_6, C_4);
  and and_37 (and_37_out, A_6, xor_10_out);
  and and_38 (and_38_out, B_6, C_4);
  and and_39 (and_39_out, not_19_out, xor_10_out);
  not not_20 (not_20_out, xor_10_out);
  or or_19 (carry_6, and_37_out, and_38_out);
  and and_40 (and_40_out, not_20_out, A_6);
  or or_20 (sum_11, and_39_out, and_40_out);
  xor xor_11 (xor_11_out, B_4, C_2);
  not not_21 (not_21_out, A_4);
  and and_41 (and_41_out, B_4, C_2);
  and and_42 (and_42_out, not_21_out, xor_11_out);
  and and_43 (and_43_out, A_4, xor_11_out);
  or or_21 (carry_4, and_43_out, and_41_out);
  not not_22 (not_22_out, xor_11_out);
  and and_44 (and_44_out, not_22_out, A_4);
  or or_22 (sum_12, and_42_out, and_44_out);
  not not_23 (not_23_out, A_5);
  xor xor_12 (xor_12_out, B_5, C_3);
  and and_45 (and_45_out, B_5, C_3);
  and and_46 (and_46_out, not_23_out, xor_12_out);
  not not_24 (not_24_out, xor_12_out);
  and and_47 (and_47_out, A_5, xor_12_out);
  or or_23 (carry_5, and_47_out, and_45_out);
  and and_48 (and_48_out, not_24_out, A_5);
  or or_24 (sum_13, and_46_out, and_48_out);
  not not_25 (not_25_out, A_7);
  xor xor_13 (xor_13_out, B_7, C_5);
  and and_49 (and_49_out, not_25_out, xor_13_out);
  and and_50 (and_50_out, A_7, xor_13_out);
  and and_51 (and_51_out, B_7, C_5);
  not not_26 (not_26_out, xor_13_out);
  or or_25 (carry_7, and_50_out, and_51_out);
  and and_52 (and_52_out, not_26_out, A_7);
  or or_26 (sum_14, and_49_out, and_52_out);
  xor xor_14 (xor_14_out, B_8, C_6);
  not not_27 (not_27_out, A_8);
  and and_53 (and_53_out, B_8, C_6);
  and and_54 (and_54_out, not_27_out, xor_14_out);
  not not_28 (not_28_out, xor_14_out);
  and and_55 (and_55_out, A_8, xor_14_out);
  or or_27 (carry_8, and_55_out, and_53_out);
  and and_56 (and_56_out, not_28_out, A_8);
  or or_28 (sum_15, and_54_out, and_56_out);

  assign {in_4[10], in_4[0]} = {2{in_4[11]}};
  assign in_14[4:0] = {5{in_4[11]}};
  // also tied to GND on the sheet: in_4[11]
endmodule

module INC_16 (
  input  [15:0] IN,
  output [15:0] OUT
);

  wire full_adder_1_carry, full_adder_2_carry, full_adder_3_carry, full_adder_4_carry, full_adder_5_carry,
       full_adder_6_carry, full_adder_7_carry, full_adder_8_carry, full_adder_9_carry, full_adder_10_carry,
       full_adder_11_carry, full_adder_12_carry, full_adder_13_carry, full_adder_14_carry,
       full_adder_15_carry, full_adder_16_carry;

  FULL_ADDER full_adder_1 (.A(IN[0]), .B(1'b1), .C(1'b0), .sum(OUT[0]), .carry(full_adder_1_carry));
  FULL_ADDER full_adder_2 (.A(IN[1]), .B(1'b0), .C(full_adder_1_carry), .sum(OUT[1]), .carry(full_adder_2_carry));
  FULL_ADDER full_adder_3 (.A(full_adder_2_carry), .B(IN[2]), .C(1'b0), .sum(OUT[2]), .carry(full_adder_3_carry));
  FULL_ADDER full_adder_4 (.A(IN[3]), .B(1'b0), .C(full_adder_3_carry), .sum(OUT[3]), .carry(full_adder_4_carry));
  FULL_ADDER full_adder_5 (.A(IN[4]), .B(1'b0), .C(full_adder_4_carry), .sum(OUT[4]), .carry(full_adder_5_carry));
  FULL_ADDER full_adder_6 (.A(IN[5]), .B(1'b0), .C(full_adder_5_carry), .sum(OUT[5]), .carry(full_adder_6_carry));
  FULL_ADDER full_adder_7 (.A(IN[6]), .B(1'b0), .C(full_adder_6_carry), .sum(OUT[6]), .carry(full_adder_7_carry));
  FULL_ADDER full_adder_8 (.A(IN[7]), .B(1'b0), .C(full_adder_7_carry), .sum(OUT[7]), .carry(full_adder_8_carry));
  FULL_ADDER full_adder_9 (.A(IN[8]), .B(1'b0), .C(full_adder_8_carry), .sum(OUT[8]), .carry(full_adder_9_carry));
  FULL_ADDER full_adder_10 (.A(IN[9]), .B(1'b0), .C(full_adder_9_carry), .sum(OUT[9]), .carry(full_adder_10_carry));
  FULL_ADDER full_adder_11 (.A(IN[10]), .B(1'b0), .C(full_adder_10_carry), .sum(OUT[10]), .carry(full_adder_11_carry));
  FULL_ADDER full_adder_12 (.A(IN[11]), .B(1'b0), .C(full_adder_11_carry), .sum(OUT[11]), .carry(full_adder_12_carry));
  FULL_ADDER full_adder_13 (.A(IN[12]), .B(1'b0), .C(full_adder_12_carry), .sum(OUT[12]), .carry(full_adder_13_carry));
  FULL_ADDER full_adder_14 (.A(IN[13]), .B(1'b0), .C(full_adder_13_carry), .sum(OUT[13]), .carry(full_adder_14_carry));
  FULL_ADDER full_adder_15 (.A(IN[14]), .B(1'b0), .C(full_adder_14_carry), .sum(OUT[14]), .carry(full_adder_15_carry));
  FULL_ADDER full_adder_16 (.A(IN[15]), .B(1'b0), .C(full_adder_15_carry), .sum(OUT[15]), .carry(full_adder_16_carry));
endmodule

module ADD4 (
  input  C,
  input  [3:0] A,
  input  [3:0] B,
  output [3:0] SUM,
  output CARRY
);

  wire full_adder_1_carry, full_adder_2_carry, full_adder_3_carry;

  FULL_ADDER full_adder_1 (.A(A[0]), .B(B[0]), .C(C), .sum(SUM[0]), .carry(full_adder_1_carry));
  FULL_ADDER full_adder_2 (.A(A[1]), .B(B[1]), .C(full_adder_1_carry), .sum(SUM[1]), .carry(full_adder_2_carry));
  FULL_ADDER full_adder_3 (.A(A[2]), .B(B[2]), .C(full_adder_2_carry), .sum(SUM[2]), .carry(full_adder_3_carry));
  FULL_ADDER full_adder_4 (.A(A[3]), .B(B[3]), .C(full_adder_3_carry), .sum(SUM[3]), .carry(CARRY));
endmodule

module tiktok (
  output out_1
);

  Clock clock_1 (.out(out_1));
endmodule

module Bit (
  input  IN,
  input  LOAD,
  output OUT
);

  wire clock_1_out, multiplexer_1_out;

  Multiplexer #(.enable("false")) multiplexer_1 (.in0(OUT), .in1(IN), .out(multiplexer_1_out), .sel(LOAD));
  Register #(.width(1)) register_1 (.D(multiplexer_1_out), .Q(OUT), .clk(clock_1_out));  // open: en, clr
  Clock clock_1 (.out(clock_1_out));
endmodule

module BIT16 (
  input  [15:0] IN,
  input  LOAD,
  output [15:0] OUT
);

  wire clock;

  Clock clock_1 (.out(clock));
  Bit bit_1 (.IN(IN[0]), .LOAD(LOAD), .OUT(OUT[0]));
  Bit bit_2 (.IN(IN[1]), .LOAD(LOAD), .OUT(OUT[1]));
  Bit bit_3 (.IN(IN[2]), .LOAD(LOAD), .OUT(OUT[2]));
  Bit bit_4 (.IN(IN[3]), .LOAD(LOAD), .OUT(OUT[3]));
  Bit bit_5 (.IN(IN[5]), .LOAD(LOAD), .OUT(OUT[5]));
  Bit bit_6 (.IN(IN[6]), .LOAD(LOAD), .OUT(OUT[6]));
  Bit bit_7 (.IN(IN[7]), .LOAD(LOAD), .OUT(OUT[7]));
  Bit bit_8 (.IN(IN[8]), .LOAD(LOAD), .OUT(OUT[8]));
  Bit bit_9 (.IN(IN[9]), .LOAD(LOAD), .OUT(OUT[9]));
  Bit bit_10 (.IN(IN[10]), .LOAD(LOAD), .OUT(OUT[10]));
  Bit bit_11 (.IN(IN[11]), .LOAD(LOAD), .OUT(OUT[11]));
  Bit bit_12 (.IN(IN[12]), .LOAD(LOAD), .OUT(OUT[12]));
  Bit bit_13 (.IN(IN[13]), .LOAD(LOAD), .OUT(OUT[13]));
  Bit bit_14 (.IN(IN[14]), .LOAD(LOAD), .OUT(OUT[14]));
  Bit bit_15 (.IN(IN[15]), .LOAD(LOAD), .OUT(OUT[15]));
  Bit bit_16 (.IN(IN[4]), .LOAD(LOAD), .OUT(OUT[4]));
endmodule

module RAM8 (
  input  [15:0] IN,
  input  LOAD,
  input  [2:0] ADDRESS,
  output [15:0] OUT
);

  wire CLOCK, dmux8_1_a, dmux8_1_b, dmux8_1_c, dmux8_1_d, dmux8_1_e, dmux8_1_f, dmux8_1_g, dmux8_1_h;
  wire [15:0] bit16_1_out, bit16_2_out, bit16_3_out, bit16_4_out, bit16_5_out, bit16_6_out, bit16_7_out,
       bit16_8_out;

  Clock u_CLOCK (.out(CLOCK));
  DMUX8 dmux8_1 (
    .IN(LOAD), .SEL_2(ADDRESS[2]), .SEL_1(ADDRESS[1]), .SEL_0(ADDRESS[0]), .A(dmux8_1_a), .B(dmux8_1_b),
    .C(dmux8_1_c), .D(dmux8_1_d), .E(dmux8_1_e), .F(dmux8_1_f), .G(dmux8_1_g), .H(dmux8_1_h));
  BIT16 bit16_1 (.IN(IN), .LOAD(dmux8_1_a), .OUT(bit16_1_out));
  BIT16 bit16_2 (.IN(IN), .LOAD(dmux8_1_b), .OUT(bit16_2_out));
  BIT16 bit16_3 (.IN(IN), .LOAD(dmux8_1_c), .OUT(bit16_3_out));
  BIT16 bit16_4 (.IN(IN), .LOAD(dmux8_1_d), .OUT(bit16_4_out));
  BIT16 bit16_5 (.IN(IN), .LOAD(dmux8_1_e), .OUT(bit16_5_out));
  BIT16 bit16_6 (.IN(IN), .LOAD(dmux8_1_f), .OUT(bit16_6_out));
  BIT16 bit16_7 (.IN(IN), .LOAD(dmux8_1_g), .OUT(bit16_7_out));
  BIT16 bit16_8 (.IN(IN), .LOAD(dmux8_1_h), .OUT(bit16_8_out));
  MUX8W16 mux8w16_1 (
    .A(bit16_1_out), .B(bit16_2_out), .C(bit16_3_out), .D(bit16_4_out), .E(bit16_5_out), .F(bit16_6_out),
    .G(bit16_7_out), .H(bit16_8_out), .SEL_0(ADDRESS[0]), .SEL_1(ADDRESS[1]), .SEL_2(ADDRESS[2]), .OUT(OUT));
endmodule

module RAM64 (
  input  [15:0] IN,
  input  LOAD,
  input  [5:0] ADDRESS,
  output [15:0] out_4
);

  wire CLOCK, dmux8_1_a, dmux8_1_b, dmux8_1_c, dmux8_1_d, dmux8_1_e, dmux8_1_f, dmux8_1_g, dmux8_1_h;
  wire [15:0] ram8_1_out, ram8_2_out, ram8_3_out, ram8_4_out, ram8_5_out, ram8_6_out, ram8_7_out, ram8_8_out;

  Clock u_CLOCK (.out(CLOCK));
  DMUX8 dmux8_1 (
    .IN(LOAD), .SEL_2(ADDRESS[5]), .SEL_1(ADDRESS[4]), .SEL_0(ADDRESS[3]), .A(dmux8_1_a), .B(dmux8_1_b),
    .C(dmux8_1_c), .D(dmux8_1_d), .E(dmux8_1_e), .F(dmux8_1_f), .G(dmux8_1_g), .H(dmux8_1_h));
  RAM8 ram8_1 (.IN(IN), .LOAD(dmux8_1_a), .ADDRESS(ADDRESS[2:0]), .OUT(ram8_1_out));
  RAM8 ram8_2 (.IN(IN), .LOAD(dmux8_1_b), .ADDRESS(ADDRESS[2:0]), .OUT(ram8_2_out));
  RAM8 ram8_3 (.IN(IN), .LOAD(dmux8_1_c), .ADDRESS(ADDRESS[2:0]), .OUT(ram8_3_out));
  RAM8 ram8_4 (.IN(IN), .LOAD(dmux8_1_d), .ADDRESS(ADDRESS[2:0]), .OUT(ram8_4_out));
  RAM8 ram8_5 (.IN(IN), .LOAD(dmux8_1_e), .ADDRESS(ADDRESS[2:0]), .OUT(ram8_5_out));
  RAM8 ram8_6 (.IN(IN), .LOAD(dmux8_1_f), .ADDRESS(ADDRESS[2:0]), .OUT(ram8_6_out));
  RAM8 ram8_7 (.IN(IN), .LOAD(dmux8_1_g), .ADDRESS(ADDRESS[2:0]), .OUT(ram8_7_out));
  RAM8 ram8_8 (.IN(IN), .LOAD(dmux8_1_h), .ADDRESS(ADDRESS[2:0]), .OUT(ram8_8_out));
  MUX8W16 mux8w16_1 (
    .A(ram8_1_out), .B(ram8_2_out), .C(ram8_3_out), .D(ram8_4_out), .E(ram8_5_out), .F(ram8_6_out),
    .G(ram8_7_out), .H(ram8_8_out), .SEL_0(ADDRESS[2]), .SEL_1(ADDRESS[1]), .SEL_2(ADDRESS[0]), .OUT(out_4));

  // Other names for the same wires on the sheet: ADDRESS__0__2[2:0] = ADDRESS[2:0]
endmodule
