// Logisim project RAM512.circ as structural Verilog: 1 circuit, main circuit main
// RAM512
module main (
  input  [15:0] IN
);

  wire CLOCK, LOAD0;
  wire [5:0] ADDRESS;
  wire [15:0] demultiplexer_1_out0, demultiplexer_1_out1, demultiplexer_1_out2, demultiplexer_1_out3,
       demultiplexer_1_out4, demultiplexer_1_out5, demultiplexer_1_out6, demultiplexer_1_out7, IN_t, OUT0,
       undriven, undriven_2, undriven_3, undriven_4, undriven_5, undriven_6, undriven_7;

  Demultiplexer #(.select(3), .width(16), .enable("false")) demultiplexer_1 (
    .out0(demultiplexer_1_out0), .out1(demultiplexer_1_out1), .out2(demultiplexer_1_out2),
    .out3(demultiplexer_1_out3), .out4(demultiplexer_1_out4), .out5(demultiplexer_1_out5),
    .out6(demultiplexer_1_out6), .out7(demultiplexer_1_out7), .in(IN));  // open: sel
  // RAM64_main main_1: pin names not known; wires that end beside it: LOAD0, ADDRESS, IN_t, CLOCK, OUT0
  // RAM64_main main_2: pin names not known; wires that end beside it: LOAD0, ADDRESS, IN_t, CLOCK, OUT0
  // RAM64_main main_3: pin names not known; wires that end beside it: LOAD0, ADDRESS, IN_t, CLOCK, OUT0
  // RAM64_main main_4: pin names not known; wires that end beside it: LOAD0, ADDRESS, IN_t, CLOCK, OUT0
  // RAM64_main main_5: pin names not known; wires that end beside it: LOAD0, ADDRESS, IN_t, CLOCK, OUT0
  // RAM64_main main_6: pin names not known; wires that end beside it: LOAD0, ADDRESS, IN_t, CLOCK, OUT0
  // RAM64_main main_7: pin names not known; wires that end beside it: LOAD0, ADDRESS, IN_t, CLOCK, OUT0
  // RAM64_main main_8: pin names not known; wires that end beside it: LOAD0, ADDRESS, IN_t, CLOCK, OUT0
  Multiplexer #(.select(3), .width(16)) multiplexer_1 (
    .in0(undriven_6), .in1(undriven_6), .in2(undriven_4), .in3(undriven_2), .in4(undriven), .in5(undriven_5),
    .in6(undriven_3), .in7(undriven_7));  // open: out, sel, en
endmodule
