// Logisim project RAM64.circ as structural Verilog: 1 circuit, main circuit main
module main (
  input  LOAD,
  input  [5:0] ADDRESS,
  input  [15:0] IN,
  output [15:0] OUT
);

  wire CLOCK, LOAD0, LOAD1, LOAD2, LOAD3, LOAD4, LOAD5, LOAD6, LOAD7;
  wire [15:0] OUT0, OUT1, OUT2, OUT3, OUT4, OUT5, OUT6, OUT7;

  Demultiplexer #(.select(3), .enable("false")) demultiplexer_1 (
    .out0(LOAD0), .out1(LOAD1), .out2(LOAD2), .out3(LOAD3), .out4(LOAD7), .out5(LOAD6), .out6(LOAD5),
    .out7(LOAD4), .in(LOAD), .sel(ADDRESS[5:3]));
  Clock u_clock (.out(CLOCK));
  RAM8 ram8_1 (.LOAD(LOAD0), .ADDRESS(ADDRESS[2:0]), .IN(IN), .OUT(OUT0));
  RAM8 ram8_2 (.LOAD(LOAD1), .ADDRESS(ADDRESS[2:0]), .IN(IN), .OUT(OUT1));
  RAM8 ram8_3 (.LOAD(LOAD2), .ADDRESS(ADDRESS[2:0]), .IN(IN), .OUT(OUT2));
  RAM8 ram8_4 (.LOAD(LOAD3), .ADDRESS(ADDRESS[2:0]), .IN(IN), .OUT(OUT3));
  RAM8 ram8_5 (.LOAD(LOAD4), .ADDRESS(ADDRESS[2:0]), .IN(IN), .OUT(OUT4));
  RAM8 ram8_6 (.LOAD(LOAD5), .ADDRESS(ADDRESS[2:0]), .IN(IN), .OUT(OUT5));
  RAM8 ram8_7 (.LOAD(LOAD6), .ADDRESS(ADDRESS[2:0]), .IN(IN), .OUT(OUT6));
  RAM8 ram8_8 (.LOAD(LOAD7), .ADDRESS(ADDRESS[2:0]), .IN(IN), .OUT(OUT7));
  Multiplexer #(.select(3), .width(16), .enable("false")) multiplexer_1 (
    .in0(OUT0), .in1(OUT1), .in2(OUT2), .in3(OUT3), .in4(OUT4), .in5(OUT5), .in6(OUT6), .in7(OUT7),
    .out(OUT), .sel(ADDRESS[5:3]));

  // Other names for the same wires on the sheet: ADDRESS_t[2:0] = ADDRESS[2:0]; ADDRESS_3__5[2:0] = ADDRESS[5:3]
endmodule
