// Logisim project RAM8.circ as structural Verilog: 1 circuit, main circuit RAM8
module RAM8 (
  input  LOAD,
  input  [2:0] ADDRESS,
  input  [15:0] IN,
  output [15:0] OUT
);

  wire CLOCK, LOAD0, LOAD1, LOAD2, LOAD3, LOAD4, LOAD5, LOAD6, LOAD7;
  wire [15:0] OUT0, OUT1, OUT2, OUT3, OUT4, OUT5, OUT6, OUT7;

  Demultiplexer #(.select(3), .enable("false")) demultiplexer_1 (
    .out0(LOAD0), .out1(LOAD1), .out2(LOAD2), .out3(LOAD3), .out4(LOAD4), .out5(LOAD5), .out6(LOAD6),
    .out7(LOAD7), .in(LOAD), .sel(ADDRESS));
  Clock u_CLOCK (.out(CLOCK));
  // BIT16 bit16_1: pin names not known; wires that end beside it: LOAD0, IN, CLOCK, OUT0
  // BIT16 bit16_2: pin names not known; wires that end beside it: LOAD0, LOAD1, IN, CLOCK, OUT1, OUT0
  // BIT16 bit16_3: pin names not known; wires that end beside it: LOAD2, IN, CLOCK, OUT2
  // BIT16 bit16_4: pin names not known; wires that end beside it: LOAD3, IN, CLOCK, OUT3
  // BIT16 bit16_5: pin names not known; wires that end beside it: LOAD4, IN, CLOCK, OUT4
  // BIT16 bit16_6: pin names not known; wires that end beside it: LOAD5, IN, CLOCK, OUT5
  // BIT16 bit16_7: pin names not known; wires that end beside it: LOAD6, IN, CLOCK, OUT6
  // BIT16 bit16_8: pin names not known; wires that end beside it: LOAD7, IN, CLOCK, OUT7
  Multiplexer #(.select(3), .width(16), .enable("false")) multiplexer_1 (
    .in0(OUT0), .in1(OUT1), .in2(OUT2), .in3(OUT3), .in4(OUT4), .in5(OUT5), .in6(OUT6), .in7(OUT7),
    .out(OUT), .sel(ADDRESS));
endmodule
